# Fritzing sketch Shield (saved by Fritzing 0.9.10b)
circuit board: 12.014cm x 6.89579cm
breadboards: 1

parts:
  IC2 = Camdenboss CTB0158-4 [part_number=CTB0158-4 package=THT]
  Logic = Camdenboss CTB0158-6 [part_number=CTB0158-6 package=THT]
  direction = Camdenboss CTB0158-6 [part_number=CTB0158-6 package=THT]
  GND_F1 = Camdenboss CTB0158-2 [part_number=CTB0158-2 package=THT]
  GND_F2 = Camdenboss CTB0158-2 [part_number=CTB0158-2 package=THT]
  limit_switch_1-12 = Camdenboss CTB0158-12 [part_number=CTB0158-12 package=THT]
  enable = Camdenboss CTB0158-6 [part_number=CTB0158-6 package=THT]
  speed = Camdenboss CTB0158-6 [part_number=CTB0158-6 package=THT]
  allarm = Camdenboss CTB0158-6 [part_number=CTB0158-6 package=THT]
  5 = female pin header, 18 pins [form="♀ (female)"]
  4 = female pin header, 18 pins [form="♀ (female)"]
  3 = female pin header, 8 pins [form="♀ (female)"]
  2 = female pin header, 8 pins [form="♀ (female)"]
  1 = female pin header, 10 pins [form="♀ (female)"]
  GND_A1_A2_A3_A4_A5 = Camdenboss CTB0158-6 [part_number=CTB0158-6 package=THT]
  R_3_5_G_G = female pin header, 8 pins [form="♀ (female)"]

nets:
  GND: IC2.pin1, Logic.pin1, Logic.pin2, GND_F1.pin1, GND_F2.pin1, 5.pin18, 4.pin18, 1.pin4, GND_A1_A2_A3_A4_A5.pin1, R_3_5_G_G.pin6, R_3_5_G_G.pin7
  5V: IC2.pin2, Logic.pin3, Logic.pin4, 5.pin1, 4.pin1, R_3_5_G_G.pin5
  N1: IC2.pin3, 3.pin8
  N2: IC2.pin4, 3.pin7
  3.3V: Logic.pin5, Logic.pin6, R_3_5_G_G.pin4
  N3: direction.pin1, 1.pin10
  N4: direction.pin2, 1.pin9
  N5: direction.pin3, 1.pin8
  N6: direction.pin4, 1.pin7
  N7: direction.pin5, 1.pin6
  N8: direction.pin6, 1.pin5
  N9: GND_F1.pin2, 5.pin2
  N10: GND_F2.pin2, 5.pin3
  N11: limit_switch_1-12.pin1, 5.pin9
  N12: limit_switch_1-12.pin2, 5.pin10
  N13: limit_switch_1-12.pin3, 5.pin11
  N14: limit_switch_1-12.pin4, 5.pin12
  N15: limit_switch_1-12.pin5, 5.pin13
  N16: limit_switch_1-12.pin6, 5.pin14
  N17: limit_switch_1-12.pin7, 4.pin14
  N18: limit_switch_1-12.pin8, 4.pin13
  N19: limit_switch_1-12.pin9, 4.pin12
  N20: limit_switch_1-12.pin10, 4.pin11
  N21: limit_switch_1-12.pin11, 4.pin10
  N22: limit_switch_1-12.pin12, 4.pin9
  N23: enable.pin1, 3.pin6
  N24: enable.pin2, 3.pin5
  N25: enable.pin3, 3.pin4
  N26: enable.pin4, 3.pin3
  N27: enable.pin5, 3.pin2
  N28: enable.pin6, 3.pin1
  N29: speed.pin1, 2.pin6
  N30: speed.pin2, 2.pin5
  N31: speed.pin3, 2.pin4
  N32: speed.pin4, 2.pin3
  N33: speed.pin5, 2.pin2
  N34: speed.pin6, 2.pin1
  N35: allarm.pin1, 4.pin8
  N36: allarm.pin2, 4.pin7
  N37: allarm.pin3, 4.pin6
  N38: allarm.pin4, 4.pin5
  N39: allarm.pin5, 4.pin4
  N40: allarm.pin6, 4.pin3
  N41: 5.pin4, GND_A1_A2_A3_A4_A5.pin2
  N42: 5.pin5, GND_A1_A2_A3_A4_A5.pin3
  N43: 5.pin6, GND_A1_A2_A3_A4_A5.pin4
  N44: 5.pin7, GND_A1_A2_A3_A4_A5.pin5
  N45: 5.pin8, GND_A1_A2_A3_A4_A5.pin6
  reset: R_3_5_G_G.pin3
  vin: R_3_5_G_G.pin8

notes:
  1
  2
  4
  5
  6
  10
  9
  11
  7
  12
  8
  3
  3v3
  5v
  gnd
  SDA
  SCL
