# Fritzing sketch closed-loop (saved by Fritzing 0.9.10b)
circuit board: 4.2cm x 4.2cm
breadboards: 1

parts:
  J3 = female pin header, 3 pins [form="♀ (female)"]
  J1 = female pin header, 4 pins [form="♀ (female)"]
  Driver = Pololu A4988 [package=SO16]
  J2 = female pin header, 4 pins [form="♀ (female)"]
  J5 = close loop - 9 pins [form=molex package=THT]
  R1 = Resistor [tolerance=±5% power=0.25 resistance=1 package=THT]
  R2 = Resistor [tolerance=±5% power=0.25 resistance=1 package=THT]
  R3 = Resistor [tolerance=±5% power=0.25 resistance=1 package=THT]
  M1 = female pin header, 2 pins [form="♀ (female)"]
  M2 = female pin header, 2 pins [form="♀ (female)"]
  M3 = female pin header, 2 pins [form="♀ (female)"]
  Part1 = Adafruit 4-channel I2C-safe Bi-directional Logic Level Converter

nets:
  GND: J3.pin1, Driver.GND, J5.pin1, R1.Pin_0, R2.Pin_0, R3.Pin_0, Part1.GND
  3V3: J3.pin3, J5.pin4, Part1.LV
  N1: J1.pin1, Driver.1B
  N2: J1.pin2, Driver.1A
  N3: J1.pin3, Driver.2A
  N4: J1.pin4, Driver.2B
  N5: Driver.ENABLE, J5.pin5
  N6: Driver.MS1, R1.Pin_1, M1.pin1
  N7: Driver.MS2, R2.Pin_1, M2.pin1
  N8: Driver.MS3, R3.Pin_1, M3.pin1
  N9: Driver.STEP, J5.pin7
  N10: Driver.DIR, J5.pin6
  5V: Driver.VDD, J5.pin3, M1.pin2, M2.pin2, M3.pin2, Part1.HV
  12V: Driver.VMOT, J5.pin2
  N11: J2.pin2, Part1.LV1
  N12: J2.pin3, Part1.LV2
  N13: J5.pin8, Part1.HV1
  N14: J5.pin9, Part1.HV2
  N15: Part1.LV4, Part1.HV4

notes:
  GND
  OUT
  VCC
  DIR
  SCL
  SDA
  GPO
  closed loop stepper
  n2048
  1 2 3 4 5 6 7 8 9

custom parts:
  close loop - 9 pins: Generic molex header
