# Fritzing sketch level-shifter-x6 (saved by Fritzing 0.9.10b)
circuit board: 8.72537cm x 6.56171cm
breadboards: 1

parts:
  Part1 = I2C level shifter bidirectional
  Part3 = I2C level shifter bidirectional
  J2 = shrouded pin header, 36 pins [form="♂ (shrouded male)"]
  J3 = female pin header, 3 pins [form="♀ (female)"]
  J4 = female pin header, 2 pins [form="♀ (female)"]
  Part4 = I2C level shifter bidirectional
  Part5 = I2C level shifter bidirectional
  Part6 = I2C level shifter bidirectional
  Part2 = I2C level shifter bidirectional
  J1 = Camdenboss CTB0158-4 [part_number=CTB0158-4 package=THT]
  J2_2 = Camdenboss CTB0158-4 [part_number=CTB0158-4 package=THT]
  J3_2 = Camdenboss CTB0158-4 [part_number=CTB0158-4 package=THT]
  J4_2 = Camdenboss CTB0158-4 [part_number=CTB0158-4 package=THT]
  J5 = Camdenboss CTB0158-4 [part_number=CTB0158-4 package=THT]
  J6 = Camdenboss CTB0158-4 [part_number=CTB0158-4 package=THT]

nets:
  N1: Part1.LV4, J2.pin30
  N2: Part1.LV3, J2.pin31
  GND: Part1.GND, Part3.GND, J2.pin18, J2.pin19, J3.pin3, Part4.GND, Part5.GND, Part6.GND, Part2.GND
  3.3V: Part1.LV, Part3.LV, J3.pin1, J4.pin2, Part4.LV, Part5.LV, Part6.LV, Part2.LV
  N3: Part1.LV2, J2.pin32
  N4: Part1.LV1, J2.pin33
  N5: Part1.HV1, J1.pin1
  N6: Part1.HV2, J1.pin2
  5V: Part1.HV, Part3.HV, J2.pin1, J2.pin36, J3.pin2, Part4.HV, Part5.HV, Part6.HV, Part2.HV
  N7: Part1.HV3, J1.pin3
  N8: Part1.HV4, J1.pin4
  N9: Part3.LV4, J2.pin26
  N10: Part3.LV3, J2.pin27
  N11: Part3.LV2, J2.pin28
  N12: Part3.LV1, J2.pin29
  N13: Part3.HV1, J2_2.pin1
  N14: Part3.HV2, J2_2.pin2
  N15: Part3.HV3, J2_2.pin3
  N16: Part3.HV4, J2_2.pin4
  N17: J2.pin4, Part2.LV4
  N18: J2.pin5, Part2.LV3
  N19: J2.pin6, Part2.LV2
  N20: J2.pin7, Part2.LV1
  N21: J2.pin8, Part4.LV4
  N22: J2.pin9, Part4.LV3
  N23: J2.pin10, Part4.LV2
  N24: J2.pin11, Part4.LV1
  N25: J2.pin12, Part6.LV4
  N26: J2.pin13, Part6.LV3
  N27: J2.pin14, Part6.LV2
  N28: J2.pin15, Part6.LV1
  N29: J2.pin17, J4.pin1
  N30: J2.pin22, Part5.LV4
  N31: J2.pin23, Part5.LV3
  N32: J2.pin24, Part5.LV2
  N33: J2.pin25, Part5.LV1
  N34: Part4.HV1, J5.pin1
  N35: Part4.HV2, J5.pin2
  N36: Part4.HV3, J5.pin3
  N37: Part4.HV4, J5.pin4
  N38: Part5.HV1, J3_2.pin1
  N39: Part5.HV2, J3_2.pin2
  N40: Part5.HV3, J3_2.pin3
  N41: Part5.HV4, J3_2.pin4
  N42: Part6.HV1, J6.pin1
  N43: Part6.HV2, J6.pin2
  N44: Part6.HV3, J6.pin3
  N45: Part6.HV4, J6.pin4
  N46: Part2.HV1, J4_2.pin1
  N47: Part2.HV2, J4_2.pin2
  N48: Part2.HV3, J4_2.pin3
  N49: Part2.HV4, J4_2.pin4

notes:
  3 5 G
  5V
  G
  ALM
  ENA
  DIR
  STP
